// Logisim project HW2.circ as structural Verilog: 1 circuit, main circuit main
module main (
  input  _1a,
  input  U,
  input  B,
  input  W,
  input  V,
  input  A,
  input  A_2,
  input  B_2,
  input  L,
  input  C,
  input  H,
  input  D,
  input  S,
  input  E,
  input  A_3,
  input  B_3,
  input  C_2,
  input  D_2,
  output out_19,
  output Y,
  output out_21,
  output E_2,
  output out_23,
  output C2,
  output C3
);

  wire and_1_out, and_2_out, and_3_out, and_4_out, and_5_out, and_6_out, and_7_out, and_8_out, and_9_out,
       and_10_out, and_11_out, and_12_out, and_13_out, and_14_out, and_15_out, not_1_out, not_2_out,
       not_3_out, not_4_out, not_5_out, not_6_out, not_7_out, not_9_out;

  not not_1 (not_1_out, W);
  not not_2 (not_2_out, B_2);
  not not_3 (not_3_out, C);
  not not_4 (not_4_out, A_3);
  and and_1 (and_1_out, not_1_out, V);
  and and_2 (and_2_out, A, not_2_out);
  and and_3 (and_3_out, not_3_out, D, E);
  not not_5 (not_5_out, B_3);
  or or_1 (out_21, U, and_1_out);
  or or_2 (out_23, and_2_out, and_3_out);
  not not_6 (not_6_out, C_2);
  not not_7 (not_7_out, D_2);
  and and_4 (and_4_out, A_3, B_3, not_6_out, not_7_out);
  and and_5 (and_5_out, not_4_out, B_3, not_6_out, D_2);
  and and_6 (and_6_out, not_4_out, not_5_out, C_2, D_2);
  and and_7 (and_7_out, not_4_out, B_3, C_2, not_7_out);
  and and_8 (and_8_out, A_3, not_5_out, not_6_out, D_2);
  and and_9 (and_9_out, A_3, not_5_out, C_2, not_7_out);
  and and_10 (and_10_out, A_3, B_3, not_6_out, D_2);
  and and_11 (and_11_out, not_4_out, B_3, C_2, D_2);
  and and_12 (and_12_out, A_3, B_3, C_2, not_7_out);
  and and_13 (and_13_out, A_3, not_5_out, C_2, D_2);
  not not_8 (Y, B);
  or or_3 (C2, and_4_out, and_5_out, and_6_out, and_7_out, and_8_out, and_9_out);
  or or_4 (C3, and_10_out, and_11_out, and_12_out, and_13_out);
  not not_9 (not_9_out, A_2);
  and and_14 (and_14_out, A_2, L);
  and and_15 (and_15_out, not_9_out, S);
  or or_5 (E_2, and_14_out, H, and_15_out);

  assign out_19 = _1a;

  // Notes on the sheet:
  //   1b)
  //   1c)
  //   2b)
  //   3)
  //   5c)
endmodule
