// Logisim project HW3.circ as structural Verilog: 1 circuit, main circuit main
module main (
  input  B,
  input  C,
  input  D,
  input  B_2,
  input  C_2,
  input  D_2,
  input  A,
  input  B_3,
  input  Cin,
  output F,
  output F_2,
  output S,
  output Cout
);

  wire and_1_out, and_2_out, nand_1_out, nand_2_out, nand_3_out, nand_4_out, nor_1_out, nor_2_out, nor_3_out,
       nor_4_out, xor_1_out;

  and and_1 (and_1_out, A, B_3);
  nand nand_1 (nand_1_out, C, C);
  nand nand_2 (nand_2_out, D, D);
  nor nor_1 (nor_1_out, C_2, C_2);
  nor nor_2 (nor_2_out, D_2, D_2);
  xor xor_1 (xor_1_out, A, B_3);
  nand nand_3 (nand_3_out, nand_1_out, nand_2_out);
  xor xor_2 (S, xor_1_out, Cin);
  and and_2 (and_2_out, xor_1_out, Cin);
  nand nand_4 (nand_4_out, B, B);
  nor nor_3 (nor_3_out, B_2, nor_1_out);
  nor nor_4 (nor_4_out, B_2, nor_2_out);
  or or_1 (Cout, and_2_out, and_1_out);
  nand nand_5 (F, nand_4_out, nand_3_out);
  nor nor_5 (F_2, nor_3_out, nor_4_out);

  // Notes on the sheet:
  //   1b)
  //   1d)
  //   3a)
endmodule
