// Logisim project AOI.circ as structural Verilog: 1 circuit, main circuit main
module main (
  input  A,
  input  B,
  input  C,
  input  A_2,
  input  B_2,
  input  C_2,
  output out_7,
  output out_8
);

  wire and_1_out, transistor_1_out, transistor_3_out;

  and and_1 (and_1_out, B, C);
  Transistor transistor_1 (.in(1'b1), .out(transistor_1_out), .gate(B_2));
  Transistor #(.\type ("n")) transistor_2 (.in(transistor_3_out), .out(out_8), .gate(B_2));
  Transistor #(.\type ("n")) transistor_3 (.in(1'b0), .out(transistor_3_out), .gate(C_2));
  nor nor_1 (out_7, A, and_1_out);
  Transistor transistor_4 (.in(1'b1), .out(transistor_1_out), .gate(C_2));
  Transistor transistor_5 (.in(transistor_1_out), .out(out_8), .gate(A_2));
  Transistor #(.\type ("n")) transistor_6 (.in(1'b0), .out(out_8), .gate(A_2));

  // Notes on the sheet:
  //   Transistor Diagram
  //   B
  //   B
  //   C
  //   Gate Diagram
  //   C
  //   A
  //   A
  //   AND-OR-INV
  //   Y
endmodule
