// Logisim project FullAdderCARRY.circ as structural Verilog: 1 circuit, main circuit main
module main (
  input  A,
  input  B,
  input  C,
  output Y
);

  wire transistor_1_out, transistor_2_out, transistor_3_out, transistor_5_out, transistor_9_out;

  Transistor transistor_1 (.in(1'b1), .out(transistor_1_out), .gate(A));
  Transistor transistor_2 (.in(transistor_1_out), .out(transistor_2_out), .gate(B));
  Transistor transistor_3 (.in(transistor_2_out), .out(transistor_3_out), .gate(A));
  Transistor #(.\type ("n")) transistor_4 (.in(transistor_5_out), .out(transistor_3_out), .gate(A));
  Transistor #(.\type ("n")) transistor_5 (.in(1'b0), .out(transistor_5_out), .gate(B));
  Transistor transistor_6 (.in(1'b1), .out(transistor_1_out), .gate(B));
  Transistor transistor_7 (.in(transistor_1_out), .out(transistor_3_out), .gate(C));
  Transistor #(.\type ("n")) transistor_8 (.in(transistor_9_out), .out(transistor_3_out), .gate(C));
  Transistor #(.\type ("n")) transistor_9 (.in(1'b0), .out(transistor_9_out), .gate(A));
  Transistor #(.\type ("n")) transistor_10 (.in(1'b0), .out(transistor_9_out), .gate(B));
  not not_1 (Y, transistor_3_out);

  // Notes on the sheet:
  //   A
  //   B
  //   A
  //   A
  //   B
  //   VDD
  //   B
  //   C
  //   A
  //   VSS
  //   C
  //   B
endmodule
