// Logisim project OAI.circ as structural Verilog: 1 circuit, main circuit main
module main (
  input  A,
  input  B,
  input  C,
  input  A_2,
  input  B_2,
  input  C_2,
  output out_7,
  output out_8
);

  wire or_1_out, transistor_1_out, transistor_6_out;

  nand nand_1 (out_7, A, or_1_out);
  or or_1 (or_1_out, B, C);
  Transistor transistor_1 (.in(1'b1), .out(transistor_1_out), .gate(B_2));
  Transistor #(.\type ("n")) transistor_2 (.in(transistor_6_out), .out(out_8), .gate(B_2));
  Transistor transistor_3 (.in(transistor_1_out), .out(out_8), .gate(C_2));
  Transistor transistor_4 (.in(1'b1), .out(out_8), .gate(A_2));
  Transistor #(.\type ("n")) transistor_5 (.in(transistor_6_out), .out(out_8), .gate(C_2));
  Transistor #(.\type ("n")) transistor_6 (.in(1'b0), .out(transistor_6_out), .gate(A_2));

  // Notes on the sheet:
  //   B
  //   C
  //   B
  //   Transistor Diagram
  //   VDD
  //   A
  //   C
  //   A
  //   VSS
  //   Gate Diagram
  //   OR-AND-INVERT
endmodule
