// Logisim project MILESTONE 2.circ as structural Verilog: 3 circuits, main circuit main
module main (
  input  in_1
);

  wire and_1_out, and_2_out, clock_1_out, display_1_a, display_1_b, display_1_c, display_1_d, display_1_e,
       display_1_f, display_1_g, display_2_a, display_2_b, display_2_c, display_2_d, display_2_e,
       display_2_f, display_2_g, n4_bit_counter_1_qa, n4_bit_counter_1_qb, n4_bit_counter_1_qc,
       n4_bit_counter_1_qd, n4_bit_counter_2_qa, n4_bit_counter_2_qb, n4_bit_counter_2_qc,
       n4_bit_counter_2_qd;

  _4_bit_Counter u_4_bit_counter_1 (
    .ON_OFF(in_1), .RST(and_1_out), .CLK(and_2_out), .Qb(n4_bit_counter_1_qb), .Qc(n4_bit_counter_1_qc),
    .Qa(n4_bit_counter_1_qa), .Qd(n4_bit_counter_1_qd));
  and and_1 (and_1_out, n4_bit_counter_1_qc, n4_bit_counter_1_qb);
  Clock clock_1 (.out(clock_1_out));
  DISPLAY display_1 (
    .I1(n4_bit_counter_1_qd), .I2(n4_bit_counter_1_qc), .I3(n4_bit_counter_1_qb), .I4(n4_bit_counter_1_qa),
    .A(display_1_a), .B(display_1_b), .C(display_1_c), .D(display_1_d), .E(display_1_e), .F(display_1_f),
    .G(display_1_g));
  _7_Segment_Display u_7_segment_display_1 (
    .g(display_1_g), .f(display_1_f), .a(display_1_a), .b(display_1_b), .e(display_1_e), .d(display_1_d),
    .c(display_1_c));  // open: dp
  and and_2 (and_2_out, n4_bit_counter_2_qd, n4_bit_counter_2_qb);
  _4_bit_Counter u_4_bit_counter_2 (
    .ON_OFF(in_1), .RST(and_2_out), .CLK(clock_1_out), .Qb(n4_bit_counter_2_qb), .Qc(n4_bit_counter_2_qc),
    .Qa(n4_bit_counter_2_qa), .Qd(n4_bit_counter_2_qd));
  DISPLAY display_2 (
    .I1(n4_bit_counter_2_qd), .I2(n4_bit_counter_2_qc), .I3(n4_bit_counter_2_qb), .I4(n4_bit_counter_2_qa),
    .A(display_2_a), .B(display_2_b), .C(display_2_c), .D(display_2_d), .E(display_2_e), .F(display_2_f),
    .G(display_2_g));
  _7_Segment_Display u_7_segment_display_2 (
    .g(display_2_g), .f(display_2_f), .a(display_2_a), .b(display_2_b), .e(display_2_e), .d(display_2_d),
    .c(display_2_c));  // open: dp
endmodule

module DISPLAY (
  input  I1,
  input  I2,
  input  I3,
  input  I4,
  output A,
  output B,
  output C,
  output D,
  output E,
  output F,
  output G
);

  wire and_1_out, and_2_out, and_3_out, and_4_out, and_5_out, and_6_out, and_7_out, and_8_out, and_9_out,
       and_10_out, and_11_out, and_12_out, and_13_out, and_14_out, and_15_out, and_16_out, and_17_out,
       and_18_out, and_19_out, and_20_out, and_21_out, and_22_out, and_23_out, and_24_out, and_25_out,
       and_26_out, not_1_out, not_2_out, not_3_out, not_4_out, or_1_out, or_2_out, or_3_out, or_4_out,
       or_5_out, or_6_out, or_7_out, or_8_out, or_9_out, or_10_out, or_12_out, or_13_out, or_18_out,
       or_19_out;

  not not_1 (not_1_out, I1);
  not not_2 (not_2_out, I2);
  not not_3 (not_3_out, I3);
  not not_4 (not_4_out, I4);
  and and_1 (and_1_out, not_2_out, not_4_out);
  and and_2 (and_2_out, I2, I4);
  and and_3 (and_3_out, not_1_out, not_3_out);
  and and_4 (and_4_out, not_1_out, I3);
  and and_5 (and_5_out, not_2_out, not_3_out);
  and and_6 (and_6_out, not_1_out, I4);
  and and_7 (and_7_out, not_2_out, not_4_out);
  and and_8 (and_8_out, not_2_out, I3);
  and and_9 (and_9_out, I2, not_3_out);
  and and_10 (and_10_out, not_2_out, not_4_out);
  and and_11 (and_11_out, I3, not_4_out);
  and and_12 (and_12_out, I1, I3);
  and and_13 (and_13_out, I1, I2);
  and and_14 (and_14_out, not_3_out, not_4_out);
  and and_15 (and_15_out, I2, not_3_out);
  and and_16 (and_16_out, I2, not_4_out);
  and and_17 (and_17_out, not_2_out, I3);
  and and_18 (and_18_out, I2, not_3_out);
  and and_19 (and_19_out, I2, not_4_out);
  or or_1 (or_1_out, and_1_out, I3);
  or or_2 (or_2_out, and_2_out, I1);
  and and_20 (and_20_out, not_1_out, not_2_out);
  and and_21 (and_21_out, and_3_out, not_4_out);
  and and_22 (and_22_out, not_2_out, not_3_out);
  and and_23 (and_23_out, and_4_out, I4);
  or or_3 (or_3_out, and_5_out, and_6_out);
  and and_24 (and_24_out, not_1_out, I2);
  or or_4 (or_4_out, and_7_out, and_8_out);
  and and_25 (and_25_out, I3, not_4_out);
  and and_26 (and_26_out, and_9_out, I4);
  or or_5 (or_5_out, and_10_out, and_11_out);
  or or_6 (or_6_out, and_12_out, and_13_out);
  or or_7 (or_7_out, and_14_out, and_15_out);
  or or_8 (or_8_out, and_16_out, I1);
  or or_9 (or_9_out, and_17_out, and_18_out);
  or or_10 (or_10_out, and_19_out, I1);
  or or_11 (A, or_1_out, or_2_out);
  or or_12 (or_12_out, and_20_out, and_21_out);
  or or_13 (or_13_out, and_22_out, and_23_out);
  or or_14 (C, or_3_out, and_24_out);
  or or_15 (E, or_5_out, or_6_out);
  or or_16 (F, or_7_out, or_8_out);
  or or_17 (G, or_9_out, or_10_out);
  or or_18 (or_18_out, or_4_out, and_25_out);
  or or_19 (or_19_out, and_26_out, I1);
  or or_20 (B, or_12_out, or_13_out);
  or or_21 (D, or_18_out, or_19_out);
endmodule

module _4_bit_Counter (
  input  ON_OFF,
  input  RST,
  input  CLK,
  output Qb,
  output Qc,
  output Qa,
  output Qd
);

  wire and_1_out, and_2_out;

  J_K_Flip_Flop j_k_ff_1 (.J(ON_OFF), .clk(CLK), .K(ON_OFF), .Q(Qa), .reset(RST));  // open: Qn, preset, en
  J_K_Flip_Flop j_k_ff_2 (.J(Qa), .clk(CLK), .K(Qa), .Q(Qb), .reset(RST));  // open: Qn, preset, en
  and and_1 (and_1_out, Qa, Qb);
  J_K_Flip_Flop j_k_ff_3 (.J(and_1_out), .clk(CLK), .K(and_1_out), .Q(Qc), .reset(RST));  // open: Qn, preset, en
  and and_2 (and_2_out, and_1_out, Qc);
  J_K_Flip_Flop j_k_ff_4 (.J(and_2_out), .clk(CLK), .K(and_2_out), .Q(Qd), .reset(RST));  // open: Qn, preset, en
endmodule
